// Logisim project 4BitParity.circ as structural Verilog: 4 circuits, main circuit main
module main (
  input  Halt_Enable
);

  wire and_2_out, CLK, Correct, Done_Testing, Halt, Input, not_1_out, not_2_out, not_3_out, Solution,
       YourAnswer;
  wire [6:0] counter_1_q, TestNumber;

  not not_1 (not_1_out, Correct);
  Clock clock_1 (.out(CLK));
  and and_1 (Halt, Halt_Enable, not_1_out);
  Inputs inputs_1 (.Halt(Halt), .CLK(CLK), .Input(Input), .TestNumber(TestNumber), .Done_Testing(Done_Testing));
  _4BitEvenParity u_4bitevenparity_1 (.Input(Input), .CLK(CLK), .Is_Even(YourAnswer));
  // Probe on Input
  // Probe on YourAnswer
  // Probe on Solution
  // Probe on Correct
  not not_2 (not_2_out, Halt);
  and and_2 (and_2_out, Correct, not_2_out, not_3_out);
  not not_3 (not_3_out, Done_Testing);
  Checker checker_1 (.Your_Answer(YourAnswer), .TestNumber(TestNumber), .Correct(Correct), .Solution(Solution));
  Counter #(.width(7), .max('h41), .ongoal("stay")) counter_1 (
    .count(and_2_out), .Q(counter_1_q), .clk(CLK));  // open: load, D, carry, clr
  // Probe on counter_1_q

  // Notes on the sheet:
  //   Max 65
  //   Melanie Zhang, 914337474
  //   Ryan Tong, 912327046
endmodule

module _4BitEvenParity (
  input  Input,
  input  CLK,
  output Is_Even
);

  wire even, read4, register_1_q, register_2_q, register_3_q, register_4_q, register_5_q, register_6_q,
       register_7_q, register_8_q, t_ff_1_qn, t_ff_2_qn, t_ff_3_q, xor_1_out, xor_2_out;

  Register #(.width(1)) register_1 (.D(Input), .Q(register_1_q), .clk(CLK));  // open: en, clr
  Register #(.width(1)) register_2 (.D(register_1_q), .Q(register_2_q), .clk(CLK));  // open: en, clr
  T_Flip_Flop t_ff_1 (.clk(CLK), .T(CLK), .Qn(t_ff_1_qn));  // open: Q, preset, reset, en
  Register #(.width(1)) register_3 (.D(register_2_q), .Q(register_3_q), .clk(CLK));  // open: en, clr
  Register #(.width(1)) register_4 (.D(register_3_q), .Q(register_4_q), .clk(CLK));  // open: en, clr
  T_Flip_Flop t_ff_2 (.clk(CLK), .T(t_ff_1_qn), .Qn(t_ff_2_qn));  // open: Q, preset, reset, en
  xor xor_1 (xor_1_out, register_1_q, register_2_q);
  xor xor_2 (xor_2_out, register_3_q, register_4_q);
  T_Flip_Flop t_ff_3 (.clk(CLK), .T(t_ff_2_qn), .Q(t_ff_3_q));  // open: Qn, preset, reset, en
  not not_1 (read4, t_ff_3_q);
  xnor xnor_1 (even, xor_1_out, xor_2_out);
  Register #(.width(1)) register_5 (.D(read4), .Q(register_5_q), .clk(CLK));  // open: en, clr
  Register #(.width(1)) register_6 (.D(register_5_q), .Q(register_6_q), .clk(CLK));  // open: en, clr
  Register #(.width(1)) register_7 (.D(register_6_q), .Q(register_7_q), .clk(CLK));  // open: en, clr
  Register #(.width(1)) register_8 (.D(register_7_q), .Q(register_8_q), .clk(CLK));  // open: en, clr
  and and_1 (Is_Even, register_8_q, even);

  // Other names for the same wires on the sheet: clock = CLK

  // Notes on the sheet:
  //   Melanie Zhang, 914337474
  //   Ryan Tong, 912327046
endmodule

module Inputs (
  input  Halt,
  input  CLK,
  output Input,
  output [6:0] TestNumber,
  output Done_Testing
);

  wire not_1_out;

  not not_1 (not_1_out, Halt);
  Counter #(.width(7), .max('h41), .ongoal("stay")) counter_1 (
    .count(not_1_out), .Q(TestNumber), .carry(Done_Testing), .clk(CLK));  // open: load, D, clr
  ROM #(.addrWidth(7), .dataWidth(1)) rom_1 (.addr(TestNumber), .data(Input));  // open: sel

  // Notes on the sheet:
  //   contents of rom_1 (hex, n*v repeats v):
  //   7*0 1 0 0 1 0 0 0 1 1 0 1 0 0 0 1 0 1 0 1 1 0 0 4*1 0 0 0 1 0 0 1 1 0 1 0 1 0 4*1 0 0 1 1 0 4*1 0
  //   4*1
endmodule

module Checker (
  input  Your_Answer,
  input  [6:0] TestNumber,
  output Correct,
  output Solution
);

  ROM #(.addrWidth(7), .dataWidth(1)) rom_1 (.addr(TestNumber), .data(Solution));  // open: sel
  Comparator #(.width(1)) comparator_1 (.a(Solution), .b(Your_Answer), .eq(Correct));  // open: gt, lt

  // Notes on the sheet:
  //   contents of rom_1 (hex, n*v repeats v):
  //   4*0 1 11*0 1 7*0 1 0 0 0 1 11*0 1 0 0 0 1 7*0 1 11*0 1
endmodule
