// Logisim project CPU.circ as structural Verilog: 2 circuits, main circuit CPU
module CPU (
);

  wire and_1_out, CLK, comparator_1_eq, nhalt, write;
  wire [3:0] A, A_prime, adder_1_out, adder_2_out, and_2_out, and_3_out, B, B_prime, C, data, negator_1_out,
       not_2_out, op, or_2_out, or_3_out, subtractor_1_out, subtractor_2_out, xor_1_out, xor_2_out;
  wire [4:0] counter_1_q;

  Clock clock_1 (.out(CLK));
  Comparator #(.width(4)) comparator_1 (.a(op), .b(4'b0001), .eq(comparator_1_eq));  // open: gt, lt
  not not_1 (write, comparator_1_eq);
  or or_1 (nhalt, op[0], op[1], op[2], op[3]);
  Counter #(.width(5), .max('h10), .ongoal("stay")) counter_1 (
    .Q(counter_1_q), .clk(CLK));  // open: load, D, count, carry, clr
  Subtractor #(.width(4)) subtractor_1 (.a(A_prime), .b(B), .out(subtractor_1_out));  // open: bin, bout
  Subtractor #(.width(4)) subtractor_2 (.a(A_prime), .b(B_prime), .out(subtractor_2_out));  // open: bin, bout
  ROM #(.addrWidth(5), .dataWidth(16)) rom_1 (.addr(counter_1_q), .data({op, C, A, B}));  // open: sel
  Adder #(.width(4)) adder_1 (.a(A_prime), .b(B), .out(adder_1_out));  // open: cin, cout
  // Probe on {op, C, A, B}
  Adder #(.width(4)) adder_2 (.a(A_prime), .b(B_prime), .out(adder_2_out));  // open: cin, cout
  // Probe on B
  // Probe on A
  // Probe on C
  // Probe on op
  Negator #(.width(4)) negator_1 (.in(A_prime), .out(negator_1_out));
  // Probe on C
  assign not_2_out = ~A_prime;  // NOT_Gate not_2, 4 bits wide
  assign xor_1_out = B ^ A_prime;  // XOR_Gate xor_1, 4 bits wide
  assign xor_2_out = B_prime ^ A_prime;  // XOR_Gate xor_2, 4 bits wide
  and and_1 (and_1_out, nhalt, write);
  assign or_2_out = B | A_prime;  // OR_Gate or_2, 4 bits wide
  assign or_3_out = B_prime | A_prime;  // OR_Gate or_3, 4 bits wide
  Reg_File Reg_File (
    .A(A), .B(B), .C(C), .Data_In(data), .Reg_Write(and_1_out), .CLK(CLK), .A_DATA(A_prime), .B_DATA(B_prime));
  assign and_2_out = B & A_prime;  // AND_Gate and_2, 4 bits wide
  assign and_3_out = B_prime & A_prime;  // AND_Gate and_3, 4 bits wide
  Multiplexer #(.select(4), .width(4), .enable("false")) multiplexer_1 (
    .in0(4'b0000), .in1(4'b0000), .in2(B), .in3(A_prime), .in4(and_3_out), .in5(and_2_out), .in6(or_3_out),
    .in7(or_2_out), .in8(xor_2_out), .in9(xor_1_out), .in10(not_2_out), .in11(negator_1_out),
    .in12(adder_2_out), .in13(adder_1_out), .in14(subtractor_2_out), .in15(subtractor_1_out), .out(data),
    .sel(op));

  // Notes on the sheet:
  //   Instructions
  //   contents of rom_1 (hex, n*v repeats v):
  //   2003 2106 1005 3210 4301 5433 6520 763c 8720 986f b938 ca77 db13 ec62 fd85 e05
  //   Melanie Zhang 914337474
  //   Ryan Tong 912327046
endmodule

module Reg_File (
  input  [3:0] A,
  input  [3:0] B,
  input  [3:0] C,
  input  [3:0] Data_In,
  input  Reg_Write,
  input  CLK,
  output [3:0] A_DATA,
  output [3:0] B_DATA
);

  wire Write_Reg0, Write_Reg1, Write_Reg2, Write_Reg3, Write_Reg4, Write_Reg5, Write_Reg6, Write_Reg7,
       Write_Reg8, Write_Reg9, Write_Reg10, Write_Reg11, Write_Reg12, Write_Reg13, Write_Reg14, Write_Reg15;
  wire [3:0] Reg0, Reg1, Reg2, Reg3, Reg4, Reg5, Reg6, Reg7, Reg8, Reg9, Reg10, Reg11, Reg12, Reg13, Reg14,
       Reg15;

  Demultiplexer #(.select(4), .enable("false")) demultiplexer_1 (
    .out0(Write_Reg0), .out1(Write_Reg1), .out2(Write_Reg2), .out3(Write_Reg3), .out4(Write_Reg4),
    .out5(Write_Reg5), .out6(Write_Reg6), .out7(Write_Reg7), .out8(Write_Reg8), .out9(Write_Reg9),
    .out10(Write_Reg10), .out11(Write_Reg11), .out12(Write_Reg12), .out13(Write_Reg13), .out14(Write_Reg14),
    .out15(Write_Reg15), .in(Reg_Write), .sel(C));
  // Probe on Reg0
  Register #(.width(4)) u_Reg0 (.D(Data_In), .en(Write_Reg0), .Q(Reg0), .clk(CLK));  // open: clr
  // Probe on Reg4
  Register #(.width(4)) u_Reg4 (.D(Data_In), .en(Write_Reg4), .Q(Reg4), .clk(CLK));  // open: clr
  // Probe on Reg8
  Register #(.width(4)) u_Reg8 (.D(Data_In), .en(Write_Reg8), .Q(Reg8), .clk(CLK));  // open: clr
  // Probe on Reg12
  Register #(.width(4)) u_Reg12 (.D(Data_In), .en(Write_Reg12), .Q(Reg12), .clk(CLK));  // open: clr
  // Probe on Reg1
  Register #(.width(4)) u_Reg1 (.D(Data_In), .en(Write_Reg1), .Q(Reg1), .clk(CLK));  // open: clr
  // Probe on Reg5
  Register #(.width(4)) u_Reg5 (.D(Data_In), .en(Write_Reg5), .Q(Reg5), .clk(CLK));  // open: clr
  // Probe on Reg9
  Register #(.width(4)) u_Reg9 (.D(Data_In), .en(Write_Reg9), .Q(Reg9), .clk(CLK));  // open: clr
  // Probe on Reg13
  Register #(.width(4)) u_Reg13 (.D(Data_In), .en(Write_Reg13), .Q(Reg13), .clk(CLK));  // open: clr
  Register #(.width(4)) u_Reg2 (.D(Data_In), .en(Write_Reg2), .Q(Reg2), .clk(CLK));  // open: clr
  Register #(.width(4)) u_Reg6 (.D(Data_In), .en(Write_Reg6), .Q(Reg6), .clk(CLK));  // open: clr
  Register #(.width(4)) u_Reg10 (.D(Data_In), .en(Write_Reg10), .Q(Reg10), .clk(CLK));  // open: clr
  Register #(.width(4)) u_Reg14 (.D(Data_In), .en(Write_Reg14), .Q(Reg14), .clk(CLK));  // open: clr
  // Probe on Reg2
  // Probe on Reg6
  // Probe on Reg10
  // Probe on Reg14
  // Probe on Reg3
  Register #(.width(4)) u_Reg3 (.D(Data_In), .en(Write_Reg3), .Q(Reg3), .clk(CLK));  // open: clr
  // Probe on Reg7
  Register #(.width(4)) u_Reg7 (.D(Data_In), .en(Write_Reg7), .Q(Reg7), .clk(CLK));  // open: clr
  // Probe on Reg11
  Register #(.width(4)) u_Reg11 (.D(Data_In), .en(Write_Reg11), .Q(Reg11), .clk(CLK));  // open: clr
  // Probe on Reg15
  Register #(.width(4)) u_Reg15 (.D(Data_In), .en(Write_Reg15), .Q(Reg15), .clk(CLK));  // open: clr
  Multiplexer #(.select(4), .width(4), .enable("false")) multiplexer_1 (
    .in0(Reg0), .in1(Reg1), .in2(Reg2), .in3(Reg3), .in4(Reg4), .in5(Reg5), .in6(Reg6), .in7(Reg7),
    .in8(Reg8), .in9(Reg9), .in10(Reg10), .in11(Reg11), .in12(Reg12), .in13(Reg13), .in14(Reg14),
    .in15(Reg15), .out(A_DATA), .sel(A));
  Multiplexer #(.select(4), .width(4), .enable("false")) multiplexer_2 (
    .in0(Reg0), .in1(Reg1), .in2(Reg2), .in3(Reg3), .in4(Reg4), .in5(Reg5), .in6(Reg6), .in7(Reg7),
    .in8(Reg8), .in9(Reg9), .in10(Reg10), .in11(Reg11), .in12(Reg12), .in13(Reg13), .in14(Reg14),
    .in15(Reg15), .out(B_DATA), .sel(B));
endmodule
