// Logisim project UpDownCounter.circ as structural Verilog: 4 circuits, main circuit main
module main (
  input  Halt_Enable
);

  wire and_2_out, CLK, Correct, Count_Down, Count_Up, Done_Testing, Halt, not_1_out, not_2_out, not_3_out;
  wire [2:0] Solution, Your_Answer;
  wire [5:0] counter_1_q;

  not not_1 (not_1_out, Correct);
  Clock clock_1 (.out(CLK));
  and and_1 (Halt, Halt_Enable, not_1_out);
  Inputs inputs_1 (.Halt(Halt), .CLK(CLK), .Count_Up(Count_Up), .Count_Down(Count_Down), .Done_Testing(Done_Testing));
  // Probe on Count_Up
  // Probe on Count_Down
  // Probe on Your_Answer
  // Probe on Solution
  Up_Down_Counter up_down_counter_1 (.Count_Up(Count_Up), .Count_Down(Count_Down), .CLK(CLK), .Count(Your_Answer));
  not not_2 (not_2_out, Halt);
  not not_3 (not_3_out, Done_Testing);
  Counter #(.width(6), .max('h21), .ongoal("stay")) counter_1 (
    .count(and_2_out), .Q(counter_1_q), .clk(CLK));  // open: load, D, carry, clr
  and and_2 (and_2_out, Correct, not_2_out, not_3_out);
  Checker checker_1 (
    .Halt_Enable(Halt_Enable), .Count_Up(Count_Up), .Count_Donw(Count_Down), .Your_Answer(Your_Answer),
    .CLK(CLK), .Correct(Correct), .Solution(Solution));
  // Probe on counter_1_q

  // Notes on the sheet:
  //   Your Solution in Here
  //   Max of 33
  //   Melanie Zhang, 914337474
  //   Ryan Tong, 912327046
endmodule

module Up_Down_Counter (
  input  Count_Up,
  input  Count_Down,
  input  CLK,
  output [2:0] Count
);

  wire and_1_out, and_2_out, and_3_out, and_4_out, and_5_out, and_6_out, and_7_out, Enable, nand_1_out,
       not_1_out, or_1_out, or_3_out, or_4_out, or_5_out, t_ff_1_qn, t_ff_2_qn;

  or or_1 (or_1_out, Count[0], Count[1], Count[2]);
  not not_1 (not_1_out, Count_Up);
  and and_1 (and_1_out, not_1_out, Count_Down);
  and and_2 (and_2_out, Count_Down, or_1_out);
  and and_3 (and_3_out, Count_Up, nand_1_out);
  nand nand_1 (nand_1_out, Count[0], Count[1], Count[2]);
  and and_4 (and_4_out, and_1_out, t_ff_1_qn);
  and and_5 (and_5_out, Count_Up, Count[0]);
  and and_6 (and_6_out, and_4_out, t_ff_2_qn);
  and and_7 (and_7_out, and_5_out, Count[1]);
  or or_2 (Enable, and_2_out, and_3_out);
  or or_3 (or_3_out, Count_Up, and_1_out);
  or or_4 (or_4_out, and_5_out, and_4_out);
  or or_5 (or_5_out, and_7_out, and_6_out);
  T_Flip_Flop t_ff_1 (.clk(CLK), .T(or_3_out), .Q(Count[0]), .Qn(t_ff_1_qn), .en(Enable));  // open: preset, reset
  T_Flip_Flop t_ff_2 (.clk(CLK), .T(or_4_out), .Q(Count[1]), .Qn(t_ff_2_qn), .en(Enable));  // open: preset, reset
  T_Flip_Flop t_ff_3 (.clk(CLK), .T(or_5_out), .Q(Count[2]), .en(Enable));  // open: Qn, preset, reset

  // Other names for the same wires on the sheet: CO = Count[0]; C1 = Count[1]; C2 = Count[2]; Down = Count_Down;
  //   Up = Count_Up

  // Notes on the sheet:
  //   Melanie Zhang, 914337474
  //   Ryan Tong, 912327046
endmodule

module Inputs (
  input  Halt,
  input  CLK,
  output Count_Up,
  output Count_Down,
  output Done_Testing
);

  wire not_1_out;
  wire [5:0] counter_1_q;

  not not_1 (not_1_out, Halt);
  Counter #(.width(6), .max('h21), .ongoal("stay")) counter_1 (
    .count(not_1_out), .Q(counter_1_q), .carry(Done_Testing), .clk(CLK));  // open: load, D, clr
  ROM #(.addrWidth(6), .dataWidth(2)) rom_1 (.addr(counter_1_q), .data({Count_Up, Count_Down}));  // open: sel

  // Notes on the sheet:
  //   contents of rom_1 (hex, n*v repeats v):
  //   0 2 0 2 0 2 0 2 0 2 0 2 0 2 0 2 0 1 0 1 0 1 0 1 0 1 0 1 0 1 0 1
endmodule

module Checker (
  input  Halt_Enable,
  input  Count_Up,
  input  Count_Donw,
  input  [2:0] Your_Answer,
  input  CLK,
  output Correct,
  output [2:0] Solution
);

  wire and_1_out, and_2_out, and_3_out, Gate, nHalt_Enable, or_2_out;

  not not_1 (nHalt_Enable, Halt_Enable);
  and and_1 (and_1_out, Correct, Halt_Enable);
  and and_2 (and_2_out, Count_Up, Gate);
  or or_1 (Gate, nHalt_Enable, and_1_out);
  and and_3 (and_3_out, Gate, Count_Donw);
  or or_2 (or_2_out, and_3_out, and_2_out);
  Counter #(.width(3), .max('h7), .ongoal("stay")) counter_1 (
    .load(and_3_out), .count(or_2_out), .Q(Solution), .clk(CLK));  // open: D, carry, clr
  Comparator #(.width(3)) comparator_1 (.a(Solution), .b(Your_Answer), .eq(Correct));  // open: gt, lt

  // Other names for the same wires on the sheet: Count_Down = Count_Donw
endmodule
