// Logisim project bcd.circ as structural Verilog: 4 circuits, main circuit main
module main (
);

  wire and_1_out, Checker_correct, clock_1_out, clock_2_out, clock_3_out, Not_Done, w0, w1, w2, w3;
  wire [3:0] counter_1_q;
  wire [6:0] Your_Answer;

  Inputs Inputs (.Clock(clock_1_out), .Not_Done(Not_Done), .w0(w0), .w1(w1), .w2(w2), .w3(w3));
  Clock clock_1 (.out(clock_1_out));
  part3 part3_1 (
    .w0(w3), .w1(w2), .w2(w1), .w3(w0), .a(Your_Answer[6]), .b(Your_Answer[5]), .c(Your_Answer[4]),
    .d(Your_Answer[3]), .e(Your_Answer[2]), .f(Your_Answer[1]), .g(Your_Answer[0]));
  // Probe on Your_Answer
  Checker Checker (.w0(w0), .w1(w1), .w2(w2), .w3(w3), .Your_Answer(Your_Answer), .Correct(Checker_correct));
  Shift_Register #(.length(10)) shift_register_1 (
    .shift(Not_Done), .in(Checker_correct), .clk(clock_2_out));  // open: out, load, clr, d0, q0, d1, q1, d2, q2, d3, q3, d4, q4, d5, q5, d6, q6, d7, q7, d8, q8, d9, q9
  Clock clock_2 (.out(clock_2_out));
  and and_1 (and_1_out, Checker_correct, Not_Done);
  Clock clock_3 (.out(clock_3_out));
  Counter #(.width(4), .max('hf), .ongoal("stay")) counter_1 (
    .count(and_1_out), .Q(counter_1_q), .clk(clock_3_out));  // open: load, D, carry, clr
  // Probe on counter_1_q

  // Notes on the sheet:
  //   Put Your Answer In Here
  //   Test 10
  //   Test 0
  //   Ryan Tong, 912327046 
  //   Calvin Huang, 999776364
endmodule

module part3 (
  input  w0,
  input  w1,
  input  w2,
  input  w3,
  output a,
  output b,
  output c,
  output d,
  output e,
  output f,
  output g
);

  wire and_1_out, and_2_out, and_3_out, and_4_out, and_5_out, and_6_out, and_7_out, and_8_out, and_9_out,
       and_10_out, and_11_out, and_12_out, and_13_out, and_14_out, and_15_out, and_16_out, and_17_out,
       not_1_out, not_2_out, not_3_out, not_4_out, not_5_out, not_6_out, not_7_out, not_8_out, not_9_out,
       not_10_out, not_11_out, not_12_out, not_13_out, not_14_out, not_15_out, not_16_out, not_17_out,
       not_18_out, not_19_out, not_20_out, not_21_out, or_1_out, or_2_out, or_3_out, or_4_out, or_6_out,
       or_8_out, or_9_out, or_10_out, or_11_out, or_14_out, or_15_out;

  not not_1 (not_1_out, w1);
  and and_1 (and_1_out, not_1_out, not_2_out);
  not not_2 (not_2_out, w3);
  and and_2 (and_2_out, w1, w3);
  not not_3 (not_3_out, w1);
  not not_4 (not_4_out, w2);
  and and_3 (and_3_out, not_4_out, not_5_out);
  not not_5 (not_5_out, w3);
  not not_6 (not_6_out, w2);
  or or_1 (or_1_out, not_6_out, w3);
  not not_7 (not_7_out, w1);
  and and_4 (and_4_out, not_7_out, not_8_out);
  not not_8 (not_8_out, w3);
  not not_9 (not_9_out, w1);
  and and_5 (and_5_out, not_9_out, w2);
  not not_10 (not_10_out, w3);
  and and_6 (and_6_out, w1, not_11_out);
  not not_11 (not_11_out, w2);
  not not_12 (not_12_out, w1);
  and and_7 (and_7_out, not_12_out, not_13_out);
  not not_13 (not_13_out, w3);
  and and_8 (and_8_out, w2, not_14_out);
  not not_14 (not_14_out, w3);
  not not_15 (not_15_out, w2);
  and and_9 (and_9_out, not_15_out, not_16_out);
  not not_16 (not_16_out, w3);
  and and_10 (and_10_out, w1, not_17_out);
  not not_17 (not_17_out, w2);
  and and_11 (and_11_out, w1, not_18_out);
  not not_18 (not_18_out, w3);
  not not_19 (not_19_out, w1);
  and and_12 (and_12_out, not_19_out, w2);
  and and_13 (and_13_out, w1, not_20_out);
  not not_20 (not_20_out, w2);
  and and_14 (and_14_out, w1, not_21_out);
  not not_21 (not_21_out, w3);
  or or_2 (or_2_out, and_1_out, w2);
  or or_3 (or_3_out, and_2_out, w0);
  or or_4 (or_4_out, not_3_out, and_3_out);
  and and_15 (and_15_out, w2, w3);
  or or_5 (c, or_1_out, w1);
  or or_6 (or_6_out, and_4_out, and_5_out);
  and and_16 (and_16_out, w2, not_10_out);
  and and_17 (and_17_out, and_6_out, w3);
  or or_7 (e, and_7_out, and_8_out);
  or or_8 (or_8_out, and_9_out, and_10_out);
  or or_9 (or_9_out, and_11_out, w0);
  or or_10 (or_10_out, and_12_out, and_13_out);
  or or_11 (or_11_out, and_14_out, w0);
  or or_12 (a, or_2_out, or_3_out);
  or or_13 (b, or_4_out, and_15_out);
  or or_14 (or_14_out, or_6_out, and_16_out);
  or or_15 (or_15_out, and_17_out, w0);
  or or_16 (f, or_8_out, or_9_out);
  or or_17 (g, or_10_out, or_11_out);
  or or_18 (d, or_14_out, or_15_out);

  // Notes on the sheet:
  //   Ryan Tong, 912327046
  //   Calvin Huang, 999776364
endmodule

module Inputs (
  input  Clock,
  output Not_Done,
  output w0,
  output w1,
  output w2,
  output w3
);

  wire comparator_1_eq;

  Counter #(.width(4), .max('ha), .ongoal("stay")) counter_1 (
    .count(1'b1), .Q({w3, w2, w1, w0}), .clk(Clock));  // open: load, D, carry, clr
  Comparator #(.width(4)) comparator_1 (.a(4'b1010), .b({w3, w2, w1, w0}), .eq(comparator_1_eq));  // open: gt, lt
  not not_1 (Not_Done, comparator_1_eq);
endmodule

module Checker (
  input  w0,
  input  w1,
  input  w2,
  input  w3,
  input  [6:0] Your_Answer,
  output Correct
);

  wire [6:0] rom_1_data;

  ROM #(.addrWidth(4), .dataWidth(7)) rom_1 (.addr({w3, w2, w1, w0}), .data(rom_1_data));  // open: sel
  Comparator #(.width(7)) comparator_1 (.a(rom_1_data), .b(Your_Answer), .eq(Correct));  // open: gt, lt

  // Notes on the sheet:
  //   contents of rom_1 (hex, n*v repeats v):
  //   7e 30 6d 79 33 5b 5f 70 7f 7b
endmodule
