// Logisim project himel.circ as structural Verilog: 11 circuits, main circuit main
module main (
  input  EnableTestHalting,
  output [9:0] CorrectCounter,
  output [9:0] HitCounter,
  output [9:0] MissCounter,
  output [9:0] TestNumber,
  output [7:0] ByteRead,
  output [7:0] CorrectByteRead,
  output Halt
);

  wire and_3_out, and_4_out, and_5_out, CLK, CmdIsRead, Correct, CpuRead, CpuWrite, DidContain, HaltTesting,
       MaxItersReached, MemRead, MemWrite, not_1_out, not_2_out, not_4_out, NotDoneTesting, Ok2Count,
       or_1_out, Ready;
  wire [7:0] CpuWriteValue, MemAddress;
  wire [9:0] CpuAddress;
  wire [31:0] Line2Mem, LineFromMem;

  not not_1 (not_1_out, Ready);
  Clock clock_1 (.out(CLK));
  or or_1 (or_1_out, MaxItersReached, Ready);
  Counter #(.width(4), .max('h9)) MaxClocks (
    .load(Ready), .D(4'b0001), .count(not_1_out), .carry(MaxItersReached), .clk(CLK));  // open: Q, clr
  and and_1 (HaltTesting, EnableTestHalting, CmdIsRead, not_2_out);
  not not_2 (not_2_out, Correct);
  not not_3 (NotDoneTesting, Halt);
  Inputs inputs_1 (
    .HaltTesting(HaltTesting), .Ready(or_1_out), .CLK(CLK), .Done(Halt), .Read(CpuRead), .Write(CpuWrite),
    .Address(CpuAddress), .Value(CpuWriteValue), .TestNumber(TestNumber));
  Cache cache_1 (
    .CpuAddress(CpuAddress), .CpuRead(CpuRead), .CpuWrite(CpuWrite), .CpuWriteValue(CpuWriteValue),
    .CLK(CLK), .Ready(Ready), .Contains(DidContain), .ByteRead(ByteRead), .MemAddress(MemAddress),
    .MemRead(MemRead), .MemWrite(MemWrite), .LineFromMem(LineFromMem), .Line2Mem(Line2Mem));
  // Probe on CpuRead
  // Probe on CpuWrite
  // Probe on CpuAddress
  // Probe on CpuWriteValue
  // Probe on TestNumber
  // Probe on CorrectByteRead
  // Probe on Correct
  // Probe on Ready
  // Probe on DidContain
  // Probe on ByteRead
  // Probe on MemAddress
  // Probe on MemRead
  // Probe on MemWrite
  // Probe on HitCounter
  // Probe on LineFromMem
  // Probe on Line2Mem
  not not_4 (not_4_out, HaltTesting);
  RAM #(.dataWidth(32), .bus("separate")) ram_1 (
    .addr(MemAddress), .din(Line2Mem), .data(LineFromMem), .str(MemWrite), .clk(CLK), .ld(MemRead));  // open: sel, clr
  and and_2 (Ok2Count, Ready, not_4_out, NotDoneTesting);
  and and_3 (and_3_out, Correct, Ok2Count);
  and and_4 (and_4_out, DidContain, Ok2Count);
  and and_5 (and_5_out, MemRead, NotDoneTesting);
  Checker checker_1 (
    .TestNumber(TestNumber), .YourByteRead(ByteRead), .CmdIsRead(CmdIsRead),
    .CorrectByteRead(CorrectByteRead), .Correct(Correct));
  Counter #(.width(10), .max('h3ff)) u_CorrectCounter (
    .count(and_3_out), .Q(CorrectCounter), .clk(CLK));  // open: load, D, carry, clr
  Counter #(.width(10), .max('h3ff)) u_HitCounter (
    .count(and_4_out), .Q(HitCounter), .clk(CLK));  // open: load, D, carry, clr
  Counter #(.width(10), .max('h3ff)) u_MissCounter (
    .count(and_5_out), .Q(MissCounter), .clk(CLK));  // open: load, D, carry, clr
  // Probe on CorrectCounter
  // Probe on HitCounter
  // Probe on MissCounter

  // Other names for the same wires on the sheet: DoneTesting = Halt

  // Notes on the sheet:
  //   Your Answer Inside Here
endmodule

module Cache (
  input  [9:0] CpuAddress,
  input  CpuRead,
  input  CpuWrite,
  input  [7:0] CpuWriteValue,
  input  CLK,
  input  [31:0] LineFromMem,
  output Ready,
  output Contains,
  output [7:0] ByteRead,
  output [7:0] MemAddress,
  output MemRead,
  output MemWrite,
  output [31:0] Line2Mem
);

  wire _2OR3, _4OR7, _10OR11, and_1_out, and_2_out, and_3_out, and_4_out, and_5_out, comparator_1_eq,
       comparator_2_eq, comparator_3_eq, comparator_4_eq, comparator_5_eq, comparator_6_eq, comparator_7_eq,
       Contains0, Contains1, Exec0, Exec1, fndd, MemRead0, MemRead1, MemWrite0, MemWrite1, multiplexer_7_out,
       multiplexer_8_out, multiplexer_9_out, not_1_out, not_2_out, not_3_out, or_6_out, ReadOWr, Ready_t, S0,
       s0_t, s0p, S1, s1_t, s1p, S2, s2_t, s2p, S3, s3_t, s3p, Valid0, Valid1;
  wire [7:0] Line0, Line1, MemAddress0, MemAddress1;
  wire [31:0] Line2Mem0, Line2Mem1;

  NextState NextState (
    .s3(s3_t), .s2(s2_t), .s1(s1_t), .s0(s0_t), .found(fndd), .cpuRead(CpuRead), .cpuWrite(CpuWrite),
    .S3p(s3p), .S2p(s2p), .S1p(s1p), .S0p(s0p), .ready(Ready_t));
  Register #(.width(4)) State (.D({s3p, s2p, s1p, s0p}), .Q({s3_t, s2_t, s1_t, s0_t}), .clk(CLK));  // open: en, clr
  Set Set1 (
    .CpuAddress(CpuAddress), .CpuWriteValue(CpuWriteValue), .LineFromMem(LineFromMem), .Exect(Exec1),
    .States({S3, S2, S1, S0}), .CLK(CLK), .Set(1'b1), .LineFound(Line1), .Line2Mem(Line2Mem1),
    .MemRead(MemRead1), .MemWrite(MemWrite1), .MemAddress(MemAddress1), .Contains(Contains1), .Valid(Valid1));  // open: out_10, out_9, out_12
  Set Set0 (
    .CpuAddress(CpuAddress), .CpuWriteValue(CpuWriteValue), .LineFromMem(LineFromMem), .Exect(Exec0),
    .States({S3, S2, S1, S0}), .CLK(CLK), .Set(1'b0), .LineFound(Line0), .Line2Mem(Line2Mem0),
    .MemRead(MemRead0), .MemWrite(MemWrite0), .MemAddress(MemAddress0), .Contains(Contains0), .Valid(Valid0));  // open: out_10, out_9, out_12
  Multiplexer #(.enable("false")) multiplexer_1 (.in0(1'b1), .in1(1'b0), .out(Exec0), .sel(CpuAddress[2]));
  Multiplexer #(.enable("false")) multiplexer_2 (.in0(1'b0), .in1(1'b1), .out(Exec1), .sel(CpuAddress[2]));
  not not_1 (not_1_out, Valid0);
  and and_1 (and_1_out, not_1_out, not_2_out);
  not not_2 (not_2_out, Valid1);
  Comparator #(.width(4), .mode("unsigned")) comparator_1 (
    .a({S3, S2, S1, S0}), .b(4'b0001), .eq(comparator_1_eq));  // open: gt, lt
  and and_2 (and_2_out, and_1_out, comparator_1_eq);
  Multiplexer #(.enable("false")) multiplexer_3 (.in0(Ready_t), .in1(1'b0), .out(Ready), .sel(and_2_out));
  Multiplexer #(.width(32), .enable("false")) multiplexer_4 (
    .in0(Line2Mem0), .in1(Line2Mem1), .out(Line2Mem), .sel(CpuAddress[2]));
  Multiplexer #(.width(8), .enable("false")) multiplexer_5 (
    .in0(Line0), .in1(Line1), .out(ByteRead), .sel(CpuAddress[2]));
  Multiplexer #(.width(8), .enable("false")) multiplexer_6 (
    .in0(MemAddress0), .in1(MemAddress1), .out(MemAddress), .sel(CpuAddress[2]));
  or or_1 (MemRead, MemRead0, MemRead1);
  or or_2 (MemWrite, MemWrite0, MemWrite1);
  Comparator #(.width(4), .mode("unsigned")) comparator_2 (
    .a({S3, S2, S1, S0}), .b(4'b0100), .eq(comparator_2_eq));  // open: gt, lt
  Comparator #(.width(4), .mode("unsigned")) comparator_3 (
    .a({S3, S2, S1, S0}), .b(4'b0111), .eq(comparator_3_eq));  // open: gt, lt
  Comparator #(.width(4), .mode("unsigned")) comparator_4 (
    .a({S3, S2, S1, S0}), .b(4'b1010), .eq(comparator_4_eq));  // open: gt, lt
  Comparator #(.width(4), .mode("unsigned")) comparator_5 (
    .a({S3, S2, S1, S0}), .b(4'b1011), .eq(comparator_5_eq));  // open: gt, lt
  Comparator #(.width(4), .mode("unsigned")) comparator_6 (
    .a({S3, S2, S1, S0}), .b(4'b0010), .eq(comparator_6_eq));  // open: gt, lt
  Comparator #(.width(4), .mode("unsigned")) comparator_7 (
    .a({S3, S2, S1, S0}), .b(4'b0011), .eq(comparator_7_eq));  // open: gt, lt
  Multiplexer #(.enable("false")) multiplexer_7 (.in0(Contains), .in1(1'b1), .out(multiplexer_7_out), .sel(_4OR7));
  or or_3 (_4OR7, comparator_2_eq, comparator_3_eq);
  or or_4 (_10OR11, comparator_4_eq, comparator_5_eq);
  or or_5 (_2OR3, comparator_6_eq, comparator_7_eq);
  or or_6 (or_6_out, _10OR11, _4OR7);
  Multiplexer #(.enable("false")) multiplexer_8 (
    .in0(multiplexer_7_out), .in1(1'b0), .out(multiplexer_8_out), .sel(_10OR11));
  and and_3 (and_3_out, or_6_out, not_3_out);
  Multiplexer #(.enable("false")) multiplexer_9 (
    .in0(multiplexer_8_out), .in1(1'b0), .out(multiplexer_9_out), .sel(and_3_out));
  or or_7 (ReadOWr, CpuRead, CpuWrite);
  not not_3 (not_3_out, ReadOWr);
  Register #(.width(1)) State_2 (.D(multiplexer_9_out), .Q(Contains), .clk(CLK));  // open: en, clr
  and and_4 (and_4_out, Contains0, Exec0);
  and and_5 (and_5_out, Contains1, Exec1);
  or or_8 (fndd, and_4_out, and_5_out);

  // Other names for the same wires on the sheet: set = CpuAddress[2]; rdy = Ready; States[3:0] = {S3, S2, S1, S0}
endmodule

module Inputs (
  input  HaltTesting,
  input  Ready,
  input  CLK,
  output Done,
  output Read,
  output Write,
  output [9:0] Address,
  output [7:0] Value,
  output [9:0] TestNumber
);

  wire and_1_out, not_1_out, not_2_out;

  not not_1 (not_1_out, HaltTesting);
  not not_2 (not_2_out, Done);
  Counter #(.width(10), .max('h3ff), .ongoal("stay")) u_TestNumber (
    .count(and_1_out), .Q(TestNumber), .clk(CLK));  // open: load, D, carry, clr
  and and_1 (and_1_out, not_1_out, Ready, not_2_out);
  ROM #(.addrWidth(10), .dataWidth(21)) rom_1 (
    .addr(TestNumber), .data({Done, Read, Write, Address, Value}));  // open: sel

  // Notes on the sheet:
  //   contents of rom_1 (hex, n*v repeats v):
  //   80000 80100 80200 80300 80400 80500 80600 80700 80800 80900 80a00 80b00 80c00 80d00 80e00 80f00
  //   81000 81100 81200 81300 81400 81500 81600 81700 0 100000
endmodule

module Checker (
  input  [9:0] TestNumber,
  input  [7:0] YourByteRead,
  output CmdIsRead,
  output [7:0] CorrectByteRead,
  output Correct
);

  wire comparator_1_eq;
  wire [9:0] subtractor_1_out;

  // Probe on TestNumber
  Subtractor #(.width(10)) subtractor_1 (.a(TestNumber), .b({10{1'b0}}), .out(subtractor_1_out));  // open: bin, bout
  ROM #(.addrWidth(10), .dataWidth(9)) rom_1 (
    .addr(subtractor_1_out), .data({CmdIsRead, CorrectByteRead}));  // open: sel
  Comparator #(.mode("unsigned")) comparator_1 (
    .a(YourByteRead), .b(CorrectByteRead), .eq(comparator_1_eq));  // open: gt, lt
  and and_1 (Correct, comparator_1_eq, CmdIsRead);

  // Other names for the same wires on the sheet: Test_Number[9:0] = TestNumber

  // Notes on the sheet:
  //   Read Solutions
  //   contents of rom_1 (hex, n*v repeats v):
  //   100 101 102 103 104 105 106 107 108 109 10a 10b 10c 10d 10e 10f 110 111 112 113 114 115 116 117
endmodule

module LineToEvict (
  input  [1:0] Age0,
  input  [1:0] Age1,
  input  [1:0] Age2,
  input  Valid0,
  input  Valid1,
  input  Valid2,
  input  Exec,
  input  found0,
  input  found1,
  input  found2,
  output Line0,
  output Line1,
  output Line2
);

  wire _0Age2, _1Age2, _2Age2, and_5_out, and_6_out, and_7_out, and_8_out, and_9_out, and_10_out, and_11_out,
       and_12_out, and_13_out, found, multiplexer_1_out, multiplexer_2_out, multiplexer_3_out,
       multiplexer_4_out, multiplexer_5_out, multiplexer_6_out, not_1_out, not_2_out, not_3_out, not_4_out,
       not_5_out, not_6_out, not_7_out, not_8_out, not_9_out, Valid, VF0, VF1, VF2;

  and and_1 (Valid, Valid0, Valid2);
  or or_1 (found, VF0, VF1, VF2);
  and and_2 (VF0, Valid0, found0);
  and and_3 (VF1, Valid1, found1);
  and and_4 (VF2, Valid2, found2);
  Comparator #(.width(2), .mode("unsigned")) comparator_1 (.a(Age0), .b(2'b10), .eq(_0Age2));  // open: gt, lt
  Comparator #(.width(2), .mode("unsigned")) comparator_2 (.a(Age1), .b(2'b10), .eq(_1Age2));  // open: gt, lt
  Comparator #(.width(2), .mode("unsigned")) comparator_3 (.a(Age2), .b(2'b10), .eq(_2Age2));  // open: gt, lt
  and and_5 (and_5_out, _1Age2, Exec, not_3_out, not_4_out);
  and and_6 (and_6_out, _2Age2, Exec, not_5_out, not_6_out);
  not not_1 (not_1_out, Valid);
  not not_2 (not_2_out, found);
  and and_7 (and_7_out, _0Age2, Exec, not_1_out, not_2_out);
  not not_3 (not_3_out, Valid);
  not not_4 (not_4_out, found);
  not not_5 (not_5_out, Valid);
  not not_6 (not_6_out, found);
  Multiplexer #(.enable("false")) multiplexer_1 (.in0(1'b0), .in1(1'b1), .out(multiplexer_1_out), .sel(and_7_out));
  Multiplexer #(.enable("false")) multiplexer_2 (.in0(1'b0), .in1(1'b1), .out(multiplexer_2_out), .sel(and_5_out));
  Multiplexer #(.enable("false")) multiplexer_3 (.in0(1'b0), .in1(1'b1), .out(multiplexer_3_out), .sel(and_6_out));
  and and_8 (and_8_out, Exec, _0Age2, Valid, not_9_out);
  Multiplexer #(.enable("false")) multiplexer_4 (
    .in0(multiplexer_1_out), .in1(1'b1), .out(multiplexer_4_out), .sel(and_8_out));
  not not_7 (not_7_out, found);
  and and_9 (and_9_out, Exec, _1Age2, Valid, not_7_out);
  Multiplexer #(.enable("false")) multiplexer_5 (
    .in0(multiplexer_2_out), .in1(1'b1), .out(multiplexer_5_out), .sel(and_9_out));
  not not_8 (not_8_out, found);
  and and_10 (and_10_out, Exec, _2Age2, Valid, not_8_out);
  Multiplexer #(.enable("false")) multiplexer_6 (
    .in0(multiplexer_3_out), .in1(1'b1), .out(multiplexer_6_out), .sel(and_10_out));
  not not_9 (not_9_out, found);
  and and_11 (and_11_out, Exec, VF0);
  and and_12 (and_12_out, Exec, VF1);
  Multiplexer #(.enable("false")) multiplexer_7 (.in0(multiplexer_5_out), .in1(1'b1), .out(Line1), .sel(and_12_out));
  and and_13 (and_13_out, Exec, VF2);
  Multiplexer #(.enable("false")) multiplexer_8 (.in0(multiplexer_6_out), .in1(1'b1), .out(Line2), .sel(and_13_out));
  Multiplexer #(.enable("false")) multiplexer_9 (.in0(multiplexer_4_out), .in1(1'b1), .out(Line0), .sel(and_11_out));
endmodule

module Ages (
  input  [1:0] Age0,
  input  [1:0] Age1,
  input  [1:0] Age2,
  input  [3:0] State,
  input  Evict,
  input  Found,
  input  Found0,
  input  Found1,
  input  Found2,
  output [1:0] NAge0,
  output [1:0] NAge1,
  output [1:0] NAge2
);

  wire comparator_1_eq;
  wire [1:0] NAge0_t, NAge0P, NAge1_t, NAge1P, NAge2_t, NAge2P, nextage_1_newage, nextage_2_newage,
       nextage_3_newage;

  NextAge nextage_1 (.Age(Age0), .State(State), .Evict(Evict), .NewAge(nextage_1_newage));
  NextAge nextage_2 (.Age(Age1), .State(State), .Evict(Evict), .NewAge(nextage_2_newage));
  NextAge nextage_3 (.Age(Age2), .State(State), .Evict(Evict), .NewAge(nextage_3_newage));
  howOld howold_1 (
    .Age00(Age0[1]), .Age01(Age0[0]), .Age10(Age1[1]), .Age11(Age1[0]), .Age20(Age2[1]), .Age21(Age2[0]),
    .f0(Found0), .f1(Found1), .f2(Found2), .age00P(NAge0P[1]), .age01p(NAge0P[0]), .age10p(NAge1P[1]),
    .age11p(NAge1P[0]), .age20p(NAge2P[1]), .age21p(NAge2P[0]));
  Multiplexer #(.width(2), .enable("false")) multiplexer_1 (
    .in0(nextage_1_newage), .in1(NAge0P), .out(NAge0_t), .sel(Found));
  Multiplexer #(.width(2), .enable("false")) multiplexer_2 (
    .in0(nextage_2_newage), .in1(NAge1P), .out(NAge1_t), .sel(Found));
  Multiplexer #(.width(2), .enable("false")) multiplexer_3 (
    .in0(nextage_3_newage), .in1(NAge2P), .out(NAge2_t), .sel(Found));
  Comparator #(.width(4), .mode("unsigned")) comparator_1 (
    .a(State), .b(4'b0000), .eq(comparator_1_eq));  // open: gt, lt
  Multiplexer #(.width(6), .enable("false")) multiplexer_4 (
    .in0({NAge2_t, NAge1_t, NAge0_t}), .in1(6'b000110), .out({NAge2, NAge1, NAge0}), .sel(comparator_1_eq));
endmodule

module NextAge (
  input  [1:0] Age,
  input  [3:0] State,
  input  Evict,
  output [1:0] NewAge
);

  wire and_1_out, comparator_1_eq, comparator_1_lt, or_1_out;
  wire [1:0] adder_1_out, multiplexer_1_out;

  Comparator #(.width(2), .mode("unsigned")) comparator_1 (
    .a(Age), .b(2'b01), .eq(comparator_1_eq), .lt(comparator_1_lt));  // open: gt
  or or_1 (or_1_out, comparator_1_eq, comparator_1_lt);
  Adder #(.width(2)) adder_1 (.a(Age), .b(2'b01), .out(adder_1_out));  // open: cin, cout
  and and_1 (and_1_out, or_1_out, Evict);
  Multiplexer #(.width(2), .enable("false")) multiplexer_1 (
    .in0(2'b00), .in1(adder_1_out), .out(multiplexer_1_out), .sel(and_1_out));
  Multiplexer #(.width(2), .enable("false")) multiplexer_2 (
    .in0(Age), .in1(multiplexer_1_out), .out(NewAge), .sel(Evict));
endmodule

module NextState (
  input  s3,
  input  s2,
  input  s1,
  input  s0,
  input  found,
  input  cpuRead,
  input  cpuWrite,
  output S3p,
  output S2p,
  output S1p,
  output S0p,
  output ready
);

  wire and_1_out, and_2_out, and_3_out, and_4_out, and_5_out, and_6_out, and_7_out, and_8_out, and_9_out,
       and_10_out, and_11_out, and_12_out, and_13_out, and_14_out, and_15_out, and_16_out, not_1_out,
       not_2_out, not_3_out, not_4_out, not_5_out, not_6_out, not_7_out, not_8_out, not_9_out, not_10_out,
       not_11_out, not_12_out, not_13_out, not_14_out, not_15_out, not_16_out, not_17_out, not_18_out,
       not_19_out, not_20_out, not_21_out, not_22_out, not_23_out, not_24_out;

  not not_1 (not_1_out, s1);
  not not_2 (not_2_out, s0);
  not not_3 (not_3_out, s2);
  not not_4 (not_4_out, s1);
  not not_5 (not_5_out, s3);
  not not_6 (not_6_out, s2);
  not not_7 (not_7_out, s3);
  not not_8 (not_8_out, s2);
  not not_9 (not_9_out, s3);
  not not_10 (not_10_out, s2);
  not not_11 (not_11_out, s2);
  not not_12 (not_12_out, s1);
  not not_13 (not_13_out, s1);
  not not_14 (not_14_out, s0);
  not not_15 (not_15_out, s3);
  not not_16 (not_16_out, s1);
  not not_17 (not_17_out, s0);
  not not_18 (not_18_out, s3);
  not not_19 (not_19_out, s0);
  not not_20 (not_20_out, found);
  not not_21 (not_21_out, s0);
  not not_22 (not_22_out, s3);
  not not_23 (not_23_out, s2);
  not not_24 (not_24_out, s1);
  and and_1 (and_1_out, not_1_out, s0);
  and and_2 (and_2_out, s2, s1, not_2_out);
  and and_3 (and_3_out, s3, not_3_out, not_4_out);
  and and_4 (and_4_out, s3, s2, s1);
  and and_5 (and_5_out, not_5_out, not_6_out, s0);
  and and_6 (and_6_out, not_7_out, not_8_out, s1);
  and and_7 (and_7_out, not_9_out, not_10_out, s1, s0);
  and and_8 (and_8_out, s3, not_11_out, not_12_out);
  and and_9 (and_9_out, s3, not_13_out, not_14_out);
  and and_10 (and_10_out, not_15_out, not_16_out, not_17_out);
  and and_11 (and_11_out, not_18_out, not_19_out, not_20_out);
  and and_12 (and_12_out, s1, s0, found);
  and and_13 (and_13_out, s2, not_21_out, cpuWrite);
  and and_14 (and_14_out, s2, s1);
  and and_15 (and_15_out, s3, s0);
  and and_16 (and_16_out, s3, s1);
  and and_17 (ready, not_22_out, not_23_out, not_24_out, s0);
  or or_1 (S3p, and_1_out, and_2_out, and_3_out, and_4_out);
  or or_2 (S2p, and_5_out, and_6_out);
  or or_3 (S1p, and_7_out, and_8_out, and_9_out);
  or or_4 (S0p, and_10_out, and_11_out, and_12_out, and_13_out, and_14_out, and_15_out, and_16_out);
endmodule

module Line (
  input  [31:0] NewLine,
  input  [6:0] LookingForTag,
  input  Exec,
  input  [1:0] NewAge,
  input  Clk,
  input  [1:0] Offset,
  input  [3:0] State,
  input  Set,
  input  [7:0] CpuWriteValue,
  output [1:0] Age,
  output Found,
  output Valid,
  output Dirty,
  output [31:0] Line,
  output [7:0] BiteRead,
  output [6:0] Tag,
  output MemRead,
  output MemWrite,
  output [7:0] MemAddress
);

  wire _2, _4, _4OR7, _5OR6, _7, _8OR9, _10, _10OR11, _11, and_1_out, and_2_out, and_3_out, and_4_out,
       and_5_out, and_6_out, and_7_out, and_8_out, and_9_out, and_11_out, comparator_6_eq, comparator_7_eq,
       comparator_8_eq, comparator_9_eq, comparator_10_eq, multiplexer_1_out, multiplexer_2_out,
       multiplexer_7_out, multiplexer_10_out, or_3_out;
  wire [6:0] multiplexer_4_out;
  wire [7:0] multiplexer_12_out;
  wire [31:0] LineToW, multiplexer_3_out, multiplexer_5_out, multiplexer_6_out, multiplexer_8_out, NewLineToW;

  Comparator #(.width(4), .mode("unsigned")) comparator_1 (.a(State), .b(4'b1010), .eq(_10));  // open: gt, lt
  Comparator #(.width(4), .mode("unsigned")) comparator_2 (.a(State), .b(4'b1011), .eq(_11));  // open: gt, lt
  Comparator #(.width(4), .mode("unsigned")) comparator_3 (.a(State), .b(4'b0010), .eq(_2));  // open: gt, lt
  Register #(.width(2)) u_Age (.D(NewAge), .Q(Age), .clk(Clk));  // open: en, clr
  Comparator #(.width(4), .mode("unsigned")) comparator_4 (.a(State), .b(4'b0100), .eq(_4));  // open: gt, lt
  or or_1 (_4OR7, _4, _7);
  Comparator #(.width(4), .mode("unsigned")) comparator_5 (.a(State), .b(4'b0111), .eq(_7));  // open: gt, lt
  or or_2 (_10OR11, _10, _11);
  and and_1 (and_1_out, _10, Exec);
  Multiplexer #(.enable("false")) multiplexer_1 (.in0(Dirty), .in1(1'b0), .out(multiplexer_1_out), .sel(and_1_out));
  and and_2 (and_2_out, Exec, or_3_out);
  Multiplexer #(.enable("false")) multiplexer_2 (
    .in0(multiplexer_1_out), .in1(1'b1), .out(multiplexer_2_out), .sel(and_2_out));
  and and_3 (and_3_out, Exec, _7);
  Multiplexer #(.width(32), .enable("false")) multiplexer_3 (
    .in0(Line), .in1(LineToW), .out(multiplexer_3_out), .sel(and_3_out));
  or or_3 (or_3_out, _7, _11);
  and and_4 (and_4_out, Exec, _10OR11);
  Multiplexer #(.width(7), .enable("false")) multiplexer_4 (
    .in0(Tag), .in1(LookingForTag), .out(multiplexer_4_out), .sel(and_4_out));
  Register #(.width(1)) u_Dirty (.D(multiplexer_2_out), .Q(Dirty), .clk(Clk));  // open: en, clr
  and and_5 (and_5_out, Exec, _11);
  Multiplexer #(.width(32), .enable("false")) multiplexer_5 (
    .in0(multiplexer_3_out), .in1(NewLineToW), .out(multiplexer_5_out), .sel(and_5_out));
  Register #(.width(7)) u_Tag (.D(multiplexer_4_out), .Q(Tag), .clk(Clk));  // open: en, clr
  and and_6 (and_6_out, Exec, _10);
  Multiplexer #(.width(32), .enable("false")) multiplexer_6 (
    .in0(multiplexer_5_out), .in1(NewLine), .out(multiplexer_6_out), .sel(and_6_out));
  and and_7 (and_7_out, _10OR11, Exec);
  Register #(.width(1)) u_Valid (.D(multiplexer_7_out), .Q(Valid), .clk(Clk));  // open: en, clr
  Multiplexer #(.enable("false")) multiplexer_7 (.in0(Valid), .in1(1'b1), .out(multiplexer_7_out), .sel(and_7_out));
  and and_8 (and_8_out, Exec, _4);
  Multiplexer #(.width(32), .enable("false")) multiplexer_8 (
    .in0(multiplexer_6_out), .in1(Line), .out(multiplexer_8_out), .sel(and_8_out));
  Register #(.width(32)) u_Line (.D(multiplexer_8_out), .Q(Line), .clk(Clk));  // open: en, clr
  Multiplexer #(.select(2), .width(8), .enable("false")) multiplexer_9 (
    .in0(Line[7:0]), .in1(Line[15:8]), .in2(Line[23:16]), .in3(Line[31:24]), .out(BiteRead), .sel(Offset));
  Comparator #(.width(7), .mode("unsigned")) comparator_6 (
    .a(Tag), .b(LookingForTag), .eq(comparator_6_eq));  // open: gt, lt
  Comparator #(.width(4), .mode("unsigned")) comparator_7 (
    .a(State), .b(4'b0101), .eq(comparator_7_eq));  // open: gt, lt
  Comparator #(.width(4), .mode("unsigned")) comparator_8 (
    .a(State), .b(4'b0110), .eq(comparator_8_eq));  // open: gt, lt
  and and_9 (and_9_out, _5OR6, Exec, Dirty);
  Multiplexer #(.enable("false")) multiplexer_10 (
    .in0(1'b0), .in1(1'b1), .out(multiplexer_10_out), .sel(comparator_6_eq));
  or or_4 (_5OR6, comparator_7_eq, comparator_8_eq);
  Multiplexer #(.enable("false")) multiplexer_11 (.in0(1'b0), .in1(1'b1), .out(MemWrite), .sel(and_9_out));
  and and_10 (Found, multiplexer_10_out, Valid);
  Multiplexer #(.width(8), .enable("false")) multiplexer_12 (
    .in0({8{1'b0}}), .in1({LookingForTag, Set}), .out(multiplexer_12_out), .sel(MemRead));
  Comparator #(.width(4), .mode("unsigned")) comparator_9 (
    .a(State), .b(4'b1000), .eq(comparator_9_eq));  // open: gt, lt
  Comparator #(.width(4), .mode("unsigned")) comparator_10 (
    .a(State), .b(4'b1001), .eq(comparator_10_eq));  // open: gt, lt
  Multiplexer #(.width(8), .enable("false")) multiplexer_13 (
    .in0(multiplexer_12_out), .in1({Tag, Set}), .out(MemAddress), .sel(MemWrite));
  or or_5 (_8OR9, comparator_9_eq, comparator_10_eq);
  Multiplexer #(.select(2), .width(8), .enable("false")) multiplexer_14 (
    .in0(CpuWriteValue), .in1(Line[7:0]), .in2(Line[7:0]), .in3(Line[7:0]), .out(LineToW[7:0]), .sel(Offset));
  and and_11 (and_11_out, _10OR11, Exec);
  Multiplexer #(.enable("false")) multiplexer_15 (.in0(1'b0), .in1(1'b1), .out(MemRead), .sel(and_11_out));
  Multiplexer #(.select(2), .width(8), .enable("false")) multiplexer_16 (
    .in0(Line[23:16]), .in1(Line[23:16]), .in2(CpuWriteValue), .in3(Line[23:16]), .out(LineToW[23:16]),
    .sel(Offset));
  Multiplexer #(.select(2), .width(8), .enable("false")) multiplexer_17 (
    .in0(Line[15:8]), .in1(CpuWriteValue), .in2(Line[15:8]), .in3(Line[15:8]), .out(LineToW[15:8]),
    .sel(Offset));
  Multiplexer #(.select(2), .width(8), .enable("false")) multiplexer_18 (
    .in0(Line[31:24]), .in1(Line[31:24]), .in2(Line[31:24]), .in3(CpuWriteValue), .out(LineToW[31:24]),
    .sel(Offset));
  Multiplexer #(.select(2), .width(8), .enable("false")) multiplexer_19 (
    .in0(CpuWriteValue), .in1(NewLine[7:0]), .in2(NewLine[7:0]), .in3(NewLine[7:0]), .out(NewLineToW[7:0]),
    .sel(Offset));
  Multiplexer #(.select(2), .width(8), .enable("false")) multiplexer_20 (
    .in0(NewLine[23:16]), .in1(NewLine[23:16]), .in2(CpuWriteValue), .in3(NewLine[23:16]),
    .out(NewLineToW[23:16]), .sel(Offset));
  Multiplexer #(.select(2), .width(8), .enable("false")) multiplexer_21 (
    .in0(NewLine[15:8]), .in1(CpuWriteValue), .in2(NewLine[15:8]), .in3(NewLine[15:8]),
    .out(NewLineToW[15:8]), .sel(Offset));
  Multiplexer #(.select(2), .width(8), .enable("false")) multiplexer_22 (
    .in0(NewLine[31:24]), .in1(NewLine[31:24]), .in2(NewLine[31:24]), .in3(CpuWriteValue),
    .out(NewLineToW[31:24]), .sel(Offset));

  // Other names for the same wires on the sheet: ByteFound[7:0] = BiteRead; LineOut[31:0] = Line;
  //   Val0[7:0] = Line[7:0]; Val1[7:0] = Line[15:8]; Val2[7:0] = Line[23:16]; Val3[7:0] = Line[31:24];
  //   Val0P[7:0] = LineToW[7:0]; Val1P[7:0] = LineToW[15:8]; Val2P[7:0] = LineToW[23:16]; Val3P[7:0] = LineToW[31:24];
  //   MemAddressR[7:0] = {LookingForTag, Set}; MemAddressW[7:0] = {Tag, Set}; LookingFor[6:0] = LookingForTag;
  //   NVal0[7:0] = NewLine[7:0]; NVal1[7:0] = NewLine[15:8]; NVal2[7:0] = NewLine[23:16]; NVal3[7:0] = NewLine[31:24];
  //   NVal0P[7:0] = NewLineToW[7:0]; NVal1P[7:0] = NewLineToW[15:8]; NVal2P[7:0] = NewLineToW[23:16];
  //   NVal3P[7:0] = NewLineToW[31:24]
endmodule

module Set (
  input  [9:0] CpuAddress,
  input  [7:0] CpuWriteValue,
  input  [31:0] LineFromMem,
  input  Exect,
  input  [3:0] States,
  input  CLK,
  input  Set,
  output [7:0] LineFound,
  output [1:0] out_9,
  output [1:0] out_10,
  output [31:0] Line2Mem,
  output [1:0] out_12,
  output MemRead,
  output MemWrite,
  output [7:0] MemAddress,
  output Contains,
  output Valid
);

  wire _4OR7, _5OR6, _10OR11, and_1_out, and_2_out, and_3_out, and_4_out, and_5_out, and_9_out, and_10_out,
       and_11_out, comparator_1_eq, comparator_2_eq, comparator_3_eq, comparator_4_eq, comparator_5_eq,
       comparator_6_eq, comparator_7_eq, comparator_8_eq, comparator_9_eq, Dirty0, Dirty1, Dirty2, exec0,
       exec1, exec2, Found0, Found1, Found2, MemRead0, MemRead1, MemRead2, MemWrite0, MemWrite1, MemWrite2,
       or_5_out, or_6_out, TvsT0, TvsT1, TvsT2, Valid0, Valid1, Valid2;
  wire [1:0] Age0, Age1, Age2;
  wire [6:0] Tag0, Tag1, Tag2;
  wire [7:0] ByteRead0, ByteRead1, ByteRead2, MemAdd0, MemAdd1, MemAdd2, multiplexer_1_out,
       multiplexer_3_out, multiplexer_7_out, multiplexer_8_out;
  wire [31:0] Line0, Line1, Line2, multiplexer_2_out, multiplexer_4_out;

  and and_1 (and_1_out, _10OR11, Exect);
  and and_2 (and_2_out, _4OR7, Exect);
  Comparator #(.width(4), .mode("unsigned")) comparator_1 (
    .a(States), .b(4'b1010), .eq(comparator_1_eq));  // open: gt, lt
  Comparator #(.width(4), .mode("unsigned")) comparator_2 (
    .a(States), .b(4'b1011), .eq(comparator_2_eq));  // open: gt, lt
  Comparator #(.width(4), .mode("unsigned")) comparator_3 (
    .a(States), .b(4'b0100), .eq(comparator_3_eq));  // open: gt, lt
  Comparator #(.width(4), .mode("unsigned")) comparator_4 (
    .a(States), .b(4'b0111), .eq(comparator_4_eq));  // open: gt, lt
  Ages Ages (
    .Age0(Age0), .Age1(Age1), .Age2(Age2), .State(States), .Evict(and_1_out), .Found(and_2_out),
    .Found0(Found0), .Found1(Found1), .Found2(Found2), .NAge0(out_10), .NAge1(out_9), .NAge2(out_12));
  or or_1 (_10OR11, comparator_1_eq, comparator_2_eq);
  or or_2 (_4OR7, comparator_3_eq, comparator_4_eq);
  Line u_Line0 (
    .NewLine(LineFromMem), .LookingForTag(CpuAddress[9:3]), .Exec(exec0), .NewAge(out_10), .Clk(CLK),
    .Offset(CpuAddress[1:0]), .State(States), .Set(Set), .CpuWriteValue(CpuWriteValue), .Age(Age0),
    .Found(Found0), .Valid(Valid0), .Dirty(Dirty0), .Line(Line0), .BiteRead(ByteRead0), .Tag(Tag0),
    .MemRead(MemRead0), .MemWrite(MemWrite0), .MemAddress(MemAdd0));
  Line u_Line1 (
    .NewLine(LineFromMem), .LookingForTag(CpuAddress[9:3]), .Exec(exec1), .NewAge(out_9), .Clk(CLK),
    .Offset(CpuAddress[1:0]), .State(States), .Set(Set), .CpuWriteValue(CpuWriteValue), .Age(Age1),
    .Found(Found1), .Valid(Valid1), .Dirty(Dirty1), .Line(Line1), .BiteRead(ByteRead1), .Tag(Tag1),
    .MemRead(MemRead1), .MemWrite(MemWrite1), .MemAddress(MemAdd1));
  Line u_Line2 (
    .NewLine(LineFromMem), .LookingForTag(CpuAddress[9:3]), .Exec(exec2), .NewAge(out_12), .Clk(CLK),
    .Offset(CpuAddress[1:0]), .State(States), .Set(Set), .CpuWriteValue(CpuWriteValue), .Age(Age2),
    .Found(Found2), .Valid(Valid2), .Dirty(Dirty2), .Line(Line2), .BiteRead(ByteRead2), .Tag(Tag2),
    .MemRead(MemRead2), .MemWrite(MemWrite2), .MemAddress(MemAdd2));
  and and_3 (and_3_out, Valid0, Found0);
  and and_4 (and_4_out, Valid1, Found1);
  and and_5 (and_5_out, Valid2, Found2);
  or or_3 (Contains, and_3_out, and_4_out, and_5_out);
  Comparator #(.width(7), .mode("unsigned")) comparator_5 (
    .a(CpuAddress[9:3]), .b(Tag2), .eq(comparator_5_eq));  // open: gt, lt
  and and_6 (TvsT2, comparator_5_eq, Valid2);
  Comparator #(.width(7), .mode("unsigned")) comparator_6 (
    .a(CpuAddress[9:3]), .b(Tag1), .eq(comparator_6_eq));  // open: gt, lt
  and and_7 (TvsT1, comparator_6_eq, Valid1);
  Comparator #(.width(7), .mode("unsigned")) comparator_7 (
    .a(CpuAddress[9:3]), .b(Tag0), .eq(comparator_7_eq));  // open: gt, lt
  and and_8 (TvsT0, comparator_7_eq, Valid0);
  Multiplexer #(.width(8), .enable("false")) multiplexer_1 (
    .in0({8{1'b0}}), .in1(ByteRead2), .out(multiplexer_1_out), .sel(TvsT2));
  Multiplexer #(.width(32), .enable("false")) multiplexer_2 (
    .in0({32{1'b0}}), .in1(Line2), .out(multiplexer_2_out), .sel(exec2));
  Multiplexer #(.width(8), .enable("false")) multiplexer_3 (
    .in0(multiplexer_1_out), .in1(ByteRead1), .out(multiplexer_3_out), .sel(TvsT1));
  Multiplexer #(.width(32), .enable("false")) multiplexer_4 (
    .in0(multiplexer_2_out), .in1(Line1), .out(multiplexer_4_out), .sel(exec1));
  Multiplexer #(.width(8), .enable("false")) multiplexer_5 (
    .in0(multiplexer_3_out), .in1(ByteRead0), .out(LineFound), .sel(TvsT0));
  Multiplexer #(.width(32), .enable("false")) multiplexer_6 (
    .in0(multiplexer_4_out), .in1(Line0), .out(Line2Mem), .sel(exec0));
  Comparator #(.width(4), .mode("unsigned")) comparator_8 (
    .a(States), .b(4'b0101), .eq(comparator_8_eq));  // open: gt, lt
  Comparator #(.width(4), .mode("unsigned")) comparator_9 (
    .a(States), .b(4'b0110), .eq(comparator_9_eq));  // open: gt, lt
  and and_9 (and_9_out, exec1, Valid1, Dirty1);
  or or_4 (_5OR6, comparator_8_eq, comparator_9_eq);
  or or_5 (or_5_out, exec0, exec1, exec2);
  and and_10 (and_10_out, exec0, Valid0, Dirty0);
  and and_11 (and_11_out, exec2, Valid2, Dirty2);
  and and_12 (MemRead, or_5_out, _10OR11);
  or or_6 (or_6_out, and_10_out, and_9_out, and_11_out);
  and and_13 (MemWrite, or_6_out, _5OR6);
  or or_7 (Valid, Valid0, Valid1, Valid2);
  Multiplexer #(.width(8), .enable("false")) multiplexer_7 (
    .in0({8{1'b0}}), .in1(MemAdd2), .out(multiplexer_7_out), .sel(exec2));
  Multiplexer #(.width(8), .enable("false")) multiplexer_8 (
    .in0(multiplexer_7_out), .in1(MemAdd1), .out(multiplexer_8_out), .sel(exec1));
  LineToEvict linetoevict_1 (
    .Age0(Age0), .Age1(Age1), .Age2(Age2), .Valid0(Valid0), .Valid1(Valid1), .Valid2(Valid2), .Exec(Exect),
    .found0(Found0), .found1(Found1), .found2(Found2), .Line0(exec0), .Line1(exec1), .Line2(exec2));
  Multiplexer #(.width(8), .enable("false")) multiplexer_9 (
    .in0(multiplexer_8_out), .in1(MemAdd0), .out(MemAddress), .sel(exec0));

  // Other names for the same wires on the sheet: OffSet[1:0] = CpuAddress[1:0]; NewAge0[1:0] = out_10;
  //   NewAge1[1:0] = out_9; NewAge2[1:0] = out_12; Tag[6:0] = CpuAddress[9:3]
endmodule

module howOld (
  input  Age00,
  input  Age01,
  input  Age10,
  input  Age11,
  input  Age20,
  input  Age21,
  input  f0,
  input  f1,
  input  f2,
  output age00P,
  output age01p,
  output age10p,
  output age11p,
  output age20p,
  output age21p
);

  wire and_1_out, and_2_out, and_3_out, and_4_out, and_5_out, and_6_out, and_7_out, and_8_out, and_9_out,
       and_10_out, and_11_out, and_12_out, and_13_out, and_14_out, and_15_out, and_16_out, and_17_out,
       and_18_out, not_1_out, not_2_out, not_3_out, not_4_out, not_5_out, not_6_out, not_7_out, not_8_out,
       not_9_out, not_10_out, not_11_out, not_12_out, not_13_out, not_14_out, not_15_out, not_16_out,
       not_17_out, not_18_out, not_19_out;

  not not_1 (not_1_out, Age10);
  not not_2 (not_2_out, Age11);
  not not_3 (not_3_out, Age20);
  not not_4 (not_4_out, f0);
  not not_5 (not_5_out, Age00);
  not not_6 (not_6_out, Age01);
  not not_7 (not_7_out, f0);
  not not_8 (not_8_out, Age00);
  not not_9 (not_9_out, f1);
  not not_10 (not_10_out, Age21);
  not not_11 (not_11_out, Age10);
  not not_12 (not_12_out, Age11);
  not not_13 (not_13_out, f1);
  not not_14 (not_14_out, Age10);
  not not_15 (not_15_out, Age11);
  not not_16 (not_16_out, f2);
  not not_17 (not_17_out, Age20);
  not not_18 (not_18_out, Age21);
  not not_19 (not_19_out, f2);
  and and_1 (and_1_out, not_1_out, not_2_out, f2);
  and and_2 (and_2_out, Age01, not_3_out, f1);
  and and_3 (and_3_out, Age00, not_4_out);
  and and_4 (and_4_out, not_5_out, not_6_out, not_7_out);
  and and_5 (and_5_out, Age20, f1);
  and and_6 (and_6_out, Age10, f2);
  and and_7 (and_7_out, not_8_out, Age11, f2);
  and and_8 (and_8_out, Age10, not_9_out);
  and and_9 (and_9_out, Age00, not_10_out, f0);
  and and_10 (and_10_out, not_11_out, not_12_out, not_13_out);
  and and_11 (and_11_out, Age20, f0);
  and and_12 (and_12_out, Age00, f2);
  and and_13 (and_13_out, not_14_out, not_15_out, f0);
  and and_14 (and_14_out, Age20, not_16_out);
  and and_15 (and_15_out, Age10, Age21, f1);
  and and_16 (and_16_out, not_17_out, not_18_out, not_19_out);
  and and_17 (and_17_out, Age10, f0);
  and and_18 (and_18_out, Age00, f1);
  or or_1 (age00P, and_1_out, and_2_out, and_3_out);
  or or_2 (age01p, and_4_out, and_5_out, and_6_out);
  or or_3 (age10p, and_7_out, and_8_out, and_9_out);
  or or_4 (age11p, and_10_out, and_11_out, and_12_out);
  or or_5 (age20p, and_13_out, and_14_out, and_15_out);
  or or_6 (age21p, and_16_out, and_17_out, and_18_out);
endmodule
